# Fritzing sketch rpi3_breadboard_schematics (saved by Fritzing 0.9.3b)
circuit board: 7.91634cm x 5.57388cm
breadboards: 1

parts:
  Raspberry_Pi_1 = Raspberry Pi 3 [part_number=RPI-3-V1.2]
  S_GREEN = Pushbutton [package="[THT]"]
  LED_GREEN = smd LED [color="Green (555nm)" package="1206 [SMD]"]
  R_S_GREEN = Resistor [tolerance=±5% resistance=10k package=THT]
  R_L_GREEN = Resistor [tolerance=±5% resistance=470 package=THT]

nets:
  N1: Raspberry_Pi_1.GPIO21, R_L_GREEN.Pin_0
  N2: Raspberry_Pi_1.GPIO23, S_GREEN.Pin_3, S_GREEN.Pin_4, R_S_GREEN.Pin_1
  N3: Raspberry_Pi_1.GND, S_GREEN.Pin_1, S_GREEN.Pin_2, LED_GREEN.cathode
  N4: Raspberry_Pi_1.5V, R_S_GREEN.Pin_0
  N5: LED_GREEN.anode, R_L_GREEN.Pin_1
